# Fritzing sketch 7-segment (saved by Fritzing 0.9.4)
breadboards: 1

parts:
  Part1 = Arduino Uno (Rev3)
  DI1 = 7-Segment LED Display [package=THT]
  R1 = Resistor [tolerance=±5% resistance=220 package=THT]
  R2 = 100 Ω Resistor [package=THT]
  R3 = 100 Ω Resistor [package=THT]
  R4 = 100 Ω Resistor [package=THT]
  R5 = 100 Ω Resistor [package=THT]
  R6 = 100 Ω Resistor [package=THT]
  R7 = 100 Ω Resistor [package=THT]

nets:
  N1: Part1.D1/TX, R4.Pin_1
  N2: Part1.D2, R3.Pin_1
  N3: Part1.D3_PWM, R5.Pin_1
  N4: Part1.D4, R6.Pin_0
  N5: Part1.D5_PWM, R7.Pin_0
  N6: Part1.D6_PWM, R2.Pin_0
  N7: Part1.D7, R1.Pin_0
  N8: Part1.GND, DI1.commAnode#2
  N9: DI1.cathodeE, R7.Pin_1
  N10: DI1.cathodeD, R6.Pin_1
  N11: DI1.cathodeC, R5.Pin_0
  N12: DI1.cathodeB, R3.Pin_0
  N13: DI1.cathodeA, R4.Pin_0
  N14: DI1.cathodeF, R2.Pin_1
  N15: DI1.cathodeG, R1.Pin_1

custom parts:
  100 Ω Resistor: A generic resistor (0.25W)
